// Logisim project hw2.circ as structural Verilog: 1 circuit, main circuit main
module main (
  input  A1,
  input  A0,
  input  O2,
  input  B1,
  input  O1,
  input  B0,
  input  O0,
  output L0,
  output L1,
  output L2,
  output L3,
  output L4,
  output L5,
  output L6,
  output L7,
  output S
);

  wire and_1_out, and_2_out, and_3_out, and_4_out, and_5_out, and_6_out, and_7_out, and_8_out, and_9_out,
       and_10_out, and_11_out, and_12_out, and_13_out, and_14_out, and_15_out, and_16_out, and_18_out,
       and_20_out, n3_to_8_decoder_74138_1_p3, n3_to_8_decoder_74138_1_p4, n3_to_8_decoder_74138_1_p7,
       n3_to_8_decoder_74138_1_p8, n3_to_8_decoder_74138_1_p9, n3_to_8_decoder_74138_1_p10,
       n3_to_8_decoder_74138_1_p11, n3_to_8_decoder_74138_1_p12, n3_to_8_decoder_74138_1_p13,
       n3_to_8_decoder_74138_1_p14, n4_to_1_mux_x2_74153_1_p11, n4_to_1_mux_x2_74153_1_p12,
       n4_to_1_mux_x2_74153_2_p14, n4_to_1_mux_x2_74153_2_p15, not_1_out, not_2_out, not_3_out, not_4_out,
       not_5_out, not_6_out, not_7_out, or_1_out, or_2_out, or_3_out, or_4_out, or_5_out, or_6_out, or_7_out,
       xor_1_out, xor_2_out, xor_3_out, xor_4_out, xor_5_out, xor_6_out, xor_7_out, xor_8_out;

  not not_1 (not_1_out, A1);
  not not_2 (not_2_out, A0);
  not not_3 (not_3_out, B1);
  not not_4 (not_4_out, B0);
  or or_1 (or_1_out, A0, B0);
  or or_2 (or_2_out, A1, B1);
  and and_1 (and_1_out, A0, B0);
  and and_2 (and_2_out, A1, B1);
  and and_3 (and_3_out, not_2_out, not_4_out);
  and and_4 (and_4_out, not_1_out, not_3_out);
  xor xor_1 (xor_1_out, A0, B0);
  and and_5 (and_5_out, not_2_out, B0);
  xor xor_2 (xor_2_out, A1, B1);
  and and_6 (and_6_out, A0, B0);
  xor xor_3 (xor_3_out, A1, B1);
  and and_7 (and_7_out, A1, B1);
  xor xor_4 (xor_4_out, not_1_out, B1);
  xor xor_5 (xor_5_out, not_2_out, B0);
  xor xor_6 (xor_6_out, and_5_out, xor_2_out);
  and and_8 (and_8_out, xor_1_out, or_4_out);
  and and_9 (and_9_out, not_1_out, B1);
  and and_10 (and_10_out, and_5_out, not_1_out);
  and and_11 (and_11_out, and_5_out, B1);
  xor xor_7 (xor_7_out, and_6_out, xor_3_out);
  and and_12 (and_12_out, and_6_out, xor_3_out);
  and and_13 (and_13_out, xor_4_out, xor_5_out);
  xor xor_8 (xor_8_out, xor_6_out, and_8_out);
  or or_3 (or_3_out, and_9_out, and_10_out);
  or or_4 (or_4_out, or_3_out, and_11_out);
  or or_5 (or_5_out, and_12_out, and_7_out);
  not not_5 (not_5_out, O2);
  // _4_to_1_MUX__x2___74153 #(.Facing("east")) 4_to_1_mux_x2_74153_1: pin names not known; wires that end beside it: not_2_out, not_1_out, or_1_out, and_1_out, and_3_out, xor_1_out, xor_1_out, xor_1_out, O2, not_5_out, n4_to_1_mux_x2_74153_1_p11, n4_to_1_mux_x2_74153_1_p12
  // _4_to_1_MUX__x2___74153 #(.Facing("east")) 4_to_1_mux_x2_74153_2: pin names not known; wires that end beside it: and_13_out, or_2_out, and_2_out, and_4_out, xor_2_out, xor_8_out, xor_7_out, O0, O2, O0, O1, not_5_out, O1, n4_to_1_mux_x2_74153_2_p14, n4_to_1_mux_x2_74153_2_p15, O0, O1, O2, not_5_out
  and and_14 (and_14_out, O2, O1);
  or or_6 (or_6_out, n4_to_1_mux_x2_74153_1_p11, n4_to_1_mux_x2_74153_1_p12);
  or or_7 (or_7_out, n4_to_1_mux_x2_74153_2_p14, n4_to_1_mux_x2_74153_2_p15);
  not not_6 (not_6_out, O1);
  not not_7 (not_7_out, O0);
  and and_15 (and_15_out, and_14_out, O0);
  // _3_to_8_decoder__74138 #(.Facing("east")) 3_to_8_decoder_74138_1: pin names not known; wires that end beside it: or_6_out, or_7_out, n3_to_8_decoder_74138_1_p3, n3_to_8_decoder_74138_1_p4, and_15_out, and_15_out, n3_to_8_decoder_74138_1_p7, n3_to_8_decoder_74138_1_p8, n3_to_8_decoder_74138_1_p9, n3_to_8_decoder_74138_1_p10, n3_to_8_decoder_74138_1_p11, n3_to_8_decoder_74138_1_p12, n3_to_8_decoder_74138_1_p13, n3_to_8_decoder_74138_1_p14
  and and_16 (and_16_out, O0, or_5_out);
  and and_17 (n3_to_8_decoder_74138_1_p3, and_16_out, and_18_out);
  and and_18 (and_18_out, O2, not_6_out);
  and and_19 (S, and_18_out, and_20_out);
  and and_20 (and_20_out, not_7_out, or_4_out);
  not not_8 (n3_to_8_decoder_74138_1_p4, and_15_out);
  not not_9 (L0, n3_to_8_decoder_74138_1_p7);
  not not_10 (L1, n3_to_8_decoder_74138_1_p8);
  not not_11 (L2, n3_to_8_decoder_74138_1_p9);
  not not_12 (L3, n3_to_8_decoder_74138_1_p10);
  not not_13 (L4, n3_to_8_decoder_74138_1_p11);
  not not_14 (L5, n3_to_8_decoder_74138_1_p12);
  not not_15 (L6, n3_to_8_decoder_74138_1_p13);
  not not_16 (L7, n3_to_8_decoder_74138_1_p14);
endmodule
